# Fritzing sketch Circuit (saved by Fritzing 0.8.7b)
breadboards: 1

parts:
  Part1 = Arduino Uno (Rev3)
  Part3 = HC-05 [part_number=HC-05 package="breakout board"]
  R1 = Resistor [tolerance=±5% resistance=1k package=THT]
  R2 = Resistor [tolerance=±5% resistance=2.2k package=THT]
  Part4 = SRF05 Ultrasonic Rangefinder
  Part5 = Arduino Uno (Rev3)
  Part6 = HC-05 [part_number=HC-05 package="breakout board"]
  LED1 = LED - 5mm [color="Red (633nm)" package="5 mm [THT]"]
  R3 = Resistor [tolerance=±5% resistance=1k package=THT]
  R4 = Resistor [tolerance=±5% resistance=2.2k package=THT]
  R5 = Resistor [tolerance=±5% resistance=220 package=THT]
  J1 = Basic Servo

nets:
  GND: Part1.GND, Part3.GND, R2.Pin_1, Part4.GND, Part5.GND, Part6.GND, LED1.cathode, R4.Pin_1, J1.gnd
  N1: Part1.D0/RX, Part3.TXD
  N2: Part1.D1/TX, R1.Pin_1
  N3: Part1.D2, Part4.Echo
  N4: Part1.D3_PWM, Part4.Trig
  VCC: Part1.5V, Part3.VCC, Part4.VCC, Part6.VCC, J1.vcc
  N5: Part3.RXD, R1.Pin_0, R2.Pin_0
  N6: Part5.D0/RX, Part6.TXD, R4.Pin_0
  N7: Part5.D1/TX, R3.Pin_1
  N8: Part5.D2, R5.Pin_0
  N9: Part5.D3_PWM, J1.pulse
  N10: Part6.RXD, R3.Pin_0
  N11: LED1.anode, R5.Pin_1

custom parts:
  HC-05: A commonly available HC-05 Bluetooth breakout board.
